# Fritzing sketch PotentialLeds (saved by Fritzing 0.7.0b)
breadboards: 1

parts:
  Arduino1 = Arduino
  R3 = 10000 Ω Resistor [package=THT]
  R4 = 10000 Ω Resistor [package=THT]
  R5 = 10000 Ω Resistor [package=THT]
  R6 = 10000 Ω Resistor [package=THT]
  R7 = Trimmer Potentiometer [maximum_resistance=10kΩ package=THT]
  LED3 = LED - 5mm [color="Red (633nm)" package="5 mm [THT]"]
  LED6 = LED - 5mm [color="Red (633nm)" package="5 mm [THT]"]
  LED7 = LED - 5mm [color="Red (633nm)" package="5 mm [THT]"]
  LED8 = LED - 5mm [color="Red (633nm)" package="5 mm [THT]"]

nets:
  N1: Arduino1.GND, R3.Pin_0, R4.Pin_0, R5.Pin_0, R6.Pin_0, R7.leg1
  N2: Arduino1.D13, LED8.cathode
  N3: Arduino1.D11, LED7.cathode
  N4: Arduino1.D9, LED6.cathode
  N5: Arduino1.D7, LED3.cathode
  N6: Arduino1.+5V, R7.leg2
  N7: Arduino1.A2, R7.wiper
  N8: R3.Pin_1, LED8.anode
  N9: R4.Pin_1, LED7.anode
  N10: R5.Pin_1, LED6.anode
  N11: R6.Pin_1, LED3.anode

custom parts:
  10000 Ω Resistor: A generic resistor (0.25W)

// code stored in the sketch: PotentialLeds.pde
/* Analog Read to LED
 * ------------------ 
 *
 * Enables a number of leds according to a potentiometer 
 * on pin 2. Blinks them like a maniac when value gets 
 * over 50% of potentiometers potential 
 */

int potPin = 2;
int ledPins [] = { 13, 11, 9, 7 };

static int POTMIN = 0;
static int POTMAX = 750;

int highestLedPotVal = (POTMAX - (POTMAX / sizeof(ledPins)));
boolean alert = false;
int alertOnState = HIGH;
int val = 0; 

void setup() {
  for (int i=0; i < sizeof(ledPins); i++) {
    pinMode(ledPins[i], OUTPUT);
  }
  
  Serial.begin(9600);
}

void loop() {
  val = analogRead(potPin);    // read the value from the sensor
  // Serial.println(val);   
  
  alert = (val > (POTMAX));

  if (alert) {
    if (alertOnState == HIGH) {
      alertOnState = LOW;
    } else {
      alertOnState = HIGH;
    }

    for (int i=0; i < sizeof(ledPins); i++) {
        digitalWrite(ledPins[i], alertOnState);    
    }
  } else {
    for (int i=0; i < sizeof(ledPins); i++) {    
      if (val > (highestLedPotVal / (i + 1)) ) {  
        digitalWrite(ledPins[i], HIGH);
      } else {
        digitalWrite(ledPins[i], LOW);      
      }
    }
  }  
    
  delay(100);          // not so fast!
}
